# Fritzing sketch SmartHome (saved by Fritzing 0.8.3b)

parts:
  Part1 = Arduino Uno (Rev3)  # not connected
  Part2 = Arduino Wireless SD Shield
  U1 = XBEE-1 [package=xbee-1_lock]  # not connected
  RaspberryPi1 = Raspberry Pi Model B
  Part3 = Arduino Uno (Rev3)  # not connected
  Part4 = Arduino Wireless SD Shield  # not connected
  U2 = XBEE-1 [package=xbee-1_lock]  # not connected
  Part5 = Arduino Uno (Rev3)  # not connected
  Part6 = Arduino Wireless SD Shield  # not connected
  U3 = XBEE-1 [package=xbee-1_lock]  # not connected

nets:
  N1: Part2.A4, RaspberryPi1.SDA
  N2: Part2.A5, RaspberryPi1.SCL
  GND: Part2.GND, RaspberryPi1.GND

notes:
  ARDUINO CENTRAL NODE - ID=1
  ARDUINO CHILD NODE - ID=2
  ARDUINO CHILD NODE - ID=3
  Project: SmartHome
  Author: Mario Pérez Esteso
  Web: geekytheory.com
  Mail: mario@geekytheory.com
  Add as many Arduinos as you want
  Android controlled Raspberry Pi acting as a Web server

custom parts:
  Raspberry Pi Model B: Raspberry Pi (Model B)
